# Fritzing sketch garage (saved by Fritzing 0.9.2b)
circuit board: 4.2cm x 5.8cm
breadboards: 1

parts:
  JP3 = Header 12 [package=1x12_machine-pin-header_lock.004]
  J3 = Screw terminal - 2 pins [package=THT]
  Q1 = MOSFET-NCHANNEL [package=to220v]
  LED1 = LED - 5mm [color="Red (633nm)" package="5 mm [THT]"]
  R2 = Resistor [tolerance=±5% resistance=10k package=THT]
  S2 = Toggle Switch [package=THT]
  J2 = Screw terminal - 2 pins [package=THT]
  R3 = Resistor [tolerance=±5% resistance=10k package=THT]
  Part2 = 9 Degrees of Freedom - Sensor Stick
  R4 = Photocell (LDR) [package=THT]
  R5 = Resistor [tolerance=±5% resistance=10k package=THT]
  S3 = Pushbutton [package="[THT]"]
  R6 = Resistor [tolerance=±5% resistance=10k package=THT]
  S4 = Toggle Switch [package=THT]
  Part3 = Spark Core (v1.0)
  JP2 = Header 12 [package=1x12_machine-pin-header_lock.004]

nets:
  N1: JP3.1, Part3.A0
  N2: JP3.2, Part3.A1
  N3: JP3.3, Part3.A2
  N4: JP3.4, Part3.A3
  N5: JP3.5, Part3.A4
  N6: JP3.6, Part3.A5
  N7: JP3.7, Part3.A6
  N8: JP3.8, R4.pin_0, R5.Pin_0, Part3.A7
  N9: JP3.9, Part3.TX
  N10: JP3.10, Part3.RX
  GND: JP3.11, J3.pin1, Q1.S, LED1.cathode, S2.L2, Part2.GND, Part3.GND, JP2.9
  N11: JP3.12, J2.pin1, Part3.VIN
  N12: J3.pin2, Q1.D, S2.COM
  N13: Q1.G, R2.Pin_1, R3.Pin_0, Part3.D3, JP2.4
  N14: LED1.anode, R2.Pin_0
  N15: J2.pin2, S4.L2
  N16: R3.Pin_1, R5.Pin_1, R6.Pin_0, S4.COM
  N17: Part2.SCL, Part3.D1, JP2.2
  N18: Part2.SDA, Part3.D0, JP2.1
  VCC: Part2.VCC, S3.Pin_3, S3.Pin_4, R6.Pin_1, Part3.3V3, JP2.12
  N19: R4.pin_1, Part3.3V3*, JP2.10
  N20: S3.Pin_1, S3.Pin_2, Part3.D4, JP2.5
  N21: Part3.D2, JP2.3
  N22: Part3.D5, JP2.6
  N23: Part3.D6, JP2.7
  N24: Part3.D7, JP2.8
  N25: Part3.RST, JP2.11

notes:
  +
  -
  bypass
  10k
  220
  10724
  D3
  ext
  D4
  off
  on
